// Logisim project reptile8.circ as structural Verilog: 4 circuits, main circuit main
module main (
);

  wire alu_1_out_4, ARMUX, CLK, IRLD, MEMLD, MUX, PCINC, PCLD, REGLD, undriven, ZF, ZFLD;
  wire [2:0] opcode;
  wire [5:0] ALU_OP, offset;
  wire [11:0] adder_1_out, address, addrout, counter_1_q, MEM_ADDRESS, PARTIAL_INSTRUCTION;
  wire [15:0] alu_1_result, DATA_IN, Dout, registerbank_1_dout0, registerbank_1_dout1, registerbank_1_dout2,
       registerbank_1_dout3, registerbank_1_dout4, registerbank_1_dout5, registerbank_1_dout6,
       registerbank_1_dout7;
  wire [15:12] multiplexer_4_out;
  wire [15:15] WHOLE_INSTRUCTION;

  Adder #(.width(12)) adder_1 (.a(counter_1_q), .b({ALU_OP, offset}), .out(adder_1_out));  // open: cin, cout
  Clock clock_1 (.out(CLK));
  Multiplexer #(.width(12)) multiplexer_1 (
    .in0(counter_1_q), .in1(MEM_ADDRESS), .out(address), .sel(ARMUX));  // open: en
  Counter #(.width(12), .max('hfff)) counter_1 (
    .load(PCLD), .D(adder_1_out), .count(PCINC), .Q(counter_1_q), .clk(CLK));  // open: carry, clr
  RegisterBank registerbank_1 (
    .Reg_Select(offset[2:0]), .REG_LOAD(REGLD), .DATA_IN(DATA_IN), .DOUT0(registerbank_1_dout0),
    .DOUT1(registerbank_1_dout1), .DOUT2(registerbank_1_dout2), .DOUT3(registerbank_1_dout3),
    .DOUT4(registerbank_1_dout4), .DOUT5(registerbank_1_dout5), .DOUT6(registerbank_1_dout6),
    .DOUT7(registerbank_1_dout7), .Clock(CLK));
  Register #(.width(1)) register_1 (.D(alu_1_out_4), .en(ZFLD), .Q(ZF), .clk(CLK));  // open: clr
  RAM #(.addrWidth(12), .dataWidth(16), .bus("separate")) ram_1 (
    .addr(addrout), .din(Dout), .data({WHOLE_INSTRUCTION[15], opcode, PARTIAL_INSTRUCTION}), .str(MEMLD),
    .clk(CLK));  // open: sel, ld, clr
  Hex_Digit_Display hex_digit_display_1 (.value(registerbank_1_dout0[15:12]));  // open: dp
  Hex_Digit_Display hex_digit_display_2 (.value(registerbank_1_dout0[11:8]));  // open: dp
  Multiplexer #(.select(3), .width(16)) multiplexer_2 (
    .in0(registerbank_1_dout0), .in1(registerbank_1_dout1), .in2(registerbank_1_dout2),
    .in3(registerbank_1_dout3), .in4(registerbank_1_dout4), .in5(registerbank_1_dout5),
    .in6(registerbank_1_dout6), .in7(registerbank_1_dout7), .out(Dout), .sel(ALU_OP[2:0]), .en(undriven));
  Hex_Digit_Display hex_digit_display_3 (.value(registerbank_1_dout0[3:0]));  // open: dp
  Hex_Digit_Display hex_digit_display_4 (.value(registerbank_1_dout0[7:4]));  // open: dp
  ALU alu_1 (
    .Din_1(Dout), .Din_2({multiplexer_4_out, MEM_ADDRESS}), .out_4(alu_1_out_4), .result(alu_1_result),
    .ALUOP(ALU_OP));
  Multiplexer #(.width(16)) multiplexer_3 (
    .in0(alu_1_result), .in1({WHOLE_INSTRUCTION[15], opcode, PARTIAL_INSTRUCTION}), .out(DATA_IN), .sel(MUX));  // open: en
  Multiplexer #(.select(3), .width(16)) multiplexer_4 (
    .in0(registerbank_1_dout0), .in1(registerbank_1_dout1), .in2(registerbank_1_dout2),
    .in3(registerbank_1_dout3), .in4(registerbank_1_dout4), .in5(registerbank_1_dout5),
    .in6(registerbank_1_dout6), .in7(registerbank_1_dout7), .out({multiplexer_4_out, MEM_ADDRESS}),
    .sel(offset[5:3]));  // open: en
  ControlUnit controlunit_1 (
    .clk(CLK), .PCLD(PCLD), .PCINC(PCINC), .ARMUX(ARMUX), .REGLD(REGLD), .ZFLD(ZFLD), .MUX(MUX),
    .MEMLD(MEMLD), .IRLD(IRLD), .opcode(opcode), .ZF(ZF), .LOAD(1'b1));
  Register #(.width(12)) register_2 (.D(PARTIAL_INSTRUCTION), .en(IRLD), .Q({ALU_OP, offset}), .clk(CLK));  // open: clr

  // Other names for the same wires on the sheet: R1[2:0] = offset[2:0]; R3[2:0] = offset[5:3]; offset[11:6] = ALU_OP;
  //   R2[2:0] = ALU_OP[2:0]; WHOLE_INSTRUCTION[14:0] = {opcode, PARTIAL_INSTRUCTION}
endmodule

module ALU (
  input  [15:0] Din_1,
  input  [15:0] Din_2,
  input  [5:0] ALUOP,
  output out_4,
  output [15:0] result
);

  wire [15:0] adder_1_out, adder_2_out, and_1_out, multiplexer_1_out, not_1_out, or_1_out, subtractor_1_out,
       subtractor_2_out, xor_1_out;

  Adder #(.width(16)) adder_1 (.a(Din_2), .b(16'h1), .out(adder_1_out));  // open: cin, cout
  Subtractor #(.width(16)) subtractor_1 (.a(Din_2), .b(16'h1), .out(subtractor_1_out));  // open: bin, bout
  Adder #(.width(16)) adder_2 (.a(Din_1), .b(Din_2), .out(adder_2_out));  // open: cin, cout
  Subtractor #(.width(16)) subtractor_2 (.a(Din_1), .b(Din_2), .out(subtractor_2_out));  // open: bin, bout
  assign and_1_out = Din_1 & Din_2;  // AND_Gate and_1, 16 bits wide
  assign or_1_out = Din_1 | Din_2;  // OR_Gate or_1, 16 bits wide
  assign xor_1_out = Din_1 ^ Din_2;  // XOR_Gate xor_1, 16 bits wide
  assign not_1_out = ~Din_2;  // NOT_Gate not_1, 16 bits wide
  Multiplexer #(.select(3), .width(16)) multiplexer_1 (
    .in0(not_1_out), .in1(Din_2), .in2(adder_1_out), .in3(subtractor_1_out), .out(multiplexer_1_out),
    .sel(ALUOP[2:0]));  // open: in4, in5, in6, in7, en
  Multiplexer #(.select(3), .width(16)) multiplexer_2 (
    .in0(adder_2_out), .in1(subtractor_2_out), .in2(and_1_out), .in3(or_1_out), .in4(xor_1_out),
    .in7(multiplexer_1_out), .out(result), .sel(ALUOP[5:3]));  // open: in5, in6, en
  nor zf (out_4, result[0], result[1], result[2], result[3], result[4], result[5], result[6], result[7], result[8], result[9], result[10], result[11], result[12], result[13], result[14], result[15]);
endmodule

// Register Bank
module RegisterBank (
  input  [2:0] Reg_Select,
  input  REG_LOAD,
  input  [15:0] DATA_IN,
  input  Clock,
  output [15:0] DOUT0,
  output [15:0] DOUT1,
  output [15:0] DOUT2,
  output [15:0] DOUT3,
  output [15:0] DOUT4,
  output [15:0] DOUT5,
  output [15:0] DOUT6,
  output [15:0] DOUT7
);

  wire and_1_out, and_2_out, and_3_out, and_4_out, and_5_out, and_6_out, and_7_out, and_8_out,
       decoder_1_out0, decoder_1_out1, decoder_1_out2, decoder_1_out3, decoder_1_out4, decoder_1_out5,
       decoder_1_out6, decoder_1_out7;

  Decoder #(.select(3), .enable("false")) decoder_1 (
    .out0(decoder_1_out0), .out1(decoder_1_out1), .out2(decoder_1_out2), .out3(decoder_1_out3),
    .out4(decoder_1_out4), .out5(decoder_1_out5), .out6(decoder_1_out6), .out7(decoder_1_out7),
    .sel(Reg_Select));
  and and_1 (and_1_out, decoder_1_out0, REG_LOAD);
  and and_2 (and_2_out, decoder_1_out1, REG_LOAD);
  and and_3 (and_3_out, decoder_1_out2, REG_LOAD);
  and and_4 (and_4_out, decoder_1_out3, REG_LOAD);
  and and_5 (and_5_out, decoder_1_out4, REG_LOAD);
  and and_6 (and_6_out, decoder_1_out5, REG_LOAD);
  and and_7 (and_7_out, decoder_1_out6, REG_LOAD);
  and and_8 (and_8_out, decoder_1_out7, REG_LOAD);
  Register #(.width(16)) register_1 (.D(DATA_IN), .en(and_1_out), .Q(DOUT0), .clk(Clock));  // open: clr
  Register #(.width(16)) register_2 (.D(DATA_IN), .en(and_2_out), .Q(DOUT1), .clk(Clock));  // open: clr
  Register #(.width(16)) register_3 (.D(DATA_IN), .en(and_3_out), .Q(DOUT2), .clk(Clock));  // open: clr
  Register #(.width(16)) register_4 (.D(DATA_IN), .en(and_4_out), .Q(DOUT3), .clk(Clock));  // open: clr
  Register #(.width(16)) register_5 (.D(DATA_IN), .en(and_5_out), .Q(DOUT4), .clk(Clock));  // open: clr
  Register #(.width(16)) register_6 (.D(DATA_IN), .en(and_6_out), .Q(DOUT5), .clk(Clock));  // open: clr
  Register #(.width(16)) register_7 (.D(DATA_IN), .en(and_7_out), .Q(DOUT6), .clk(Clock));  // open: clr
  Register #(.width(16)) register_8 (.D(DATA_IN), .en(and_8_out), .Q(DOUT7));  // open: clk, clr
endmodule

// CU
module ControlUnit (
  input  [2:0] opcode,
  input  ZF,
  input  clk,
  input  LOAD,
  output PCLD,
  output PCINC,
  output ARMUX,
  output REGLD,
  output ZFLD,
  output MUX,
  output MEMLD,
  output IRLD
);

  wire [1:1] and_1_out;
  wire [2:0] multiplexer_1_out, multiplexer_2_out, register_1_q;
  wire [8:8] rom_1_data;

  and and_1 (and_1_out[1], ~opcode[0], ~opcode[1], opcode[2]);  // AND_Gate
  Multiplexer #(.select(2), .width(3)) multiplexer_1 (
    .in0(opcode), .in1(opcode), .in2(3'b000), .in3(3'b101), .out(multiplexer_1_out), .sel({and_1_out[1], ZF}));  // open: en
  Multiplexer #(.width(3)) multiplexer_2 (
    .in0(3'b000), .in1(multiplexer_1_out), .out(multiplexer_2_out), .sel(rom_1_data[8]));  // open: en
  Register #(.width(3)) register_1 (.D(multiplexer_2_out), .en(LOAD), .Q(register_1_q), .clk(clk));  // open: clr
  ROM #(.addrWidth(3), .dataWidth(9)) rom_1 (
    .addr(register_1_q), .data({rom_1_data[8], PCLD, PCINC, ARMUX, REGLD, ZFLD, MUX, MEMLD, IRLD}));  // open: sel

  // Notes on the sheet:
  //   contents of rom_1 (hex, n*v repeats v):
  //   141 54 34 22 0 80 0 18
endmodule
