// Logisim project modified_bird.circ as structural Verilog: 5 circuits, main circuit Bird
module Bird (
  input  [15:0] Din,
  input  in_2,
  output [15:0] Dout,
  output [11:0] Addr
);

  wire alu_1_out_4, ARMUX1, ARMUX2, DataMux, IRLD, MEMLD, MUX, PCINC, PCLD, PCMux, REGLD, SP_minus_minus,
       SP_plus_plus, undriven, ZF, ZFLD;
  wire [5:0] ALU_OP, offset;
  wire [11:0] adder_1_out, MEM_ADDRESS, multiplexer_1_out, PCValue, SP;
  wire [15:0] alu_1_result, DATA_IN, Dout_t, registerbank_1_dout0, registerbank_1_dout1,
       registerbank_1_dout2, registerbank_1_dout3, registerbank_1_dout4, registerbank_1_dout5,
       registerbank_1_dout6, registerbank_1_dout7;
  wire [15:12] multiplexer_6_out;

  Multiplexer #(.width(12)) multiplexer_1 (
    .in0(adder_1_out), .in1(Din[11:0]), .out(multiplexer_1_out), .sel(PCMux));  // open: en
  Adder #(.width(12)) adder_1 (.a(PCValue), .b({ALU_OP, offset}), .out(adder_1_out));  // open: cin, cout
  Multiplexer #(.width(16)) multiplexer_2 (
    .in0(Dout_t), .in1({4'b0000, PCValue}), .out(Dout), .sel(DataMux));  // open: en
  Multiplexer #(.select(2), .width(12)) multiplexer_3 (
    .in0(PCValue), .in1(MEM_ADDRESS), .in2(SP), .out(Addr), .sel({ARMUX2, ARMUX1}));  // open: in3, en
  Counter #(.width(12), .max('hfff)) counter_1 (
    .load(PCLD), .D(multiplexer_1_out), .count(PCINC), .Q(PCValue), .clk(in_2));  // open: carry, clr
  RegisterBank registerbank_1 (
    .Reg_Select(offset[2:0]), .REG_LOAD(REGLD), .DATA_IN(DATA_IN), .DOUT0(registerbank_1_dout0),
    .DOUT1(registerbank_1_dout1), .DOUT2(registerbank_1_dout2), .DOUT3(registerbank_1_dout3),
    .DOUT4(registerbank_1_dout4), .DOUT5(registerbank_1_dout5), .DOUT6(registerbank_1_dout6),
    .DOUT7(registerbank_1_dout7), .Clock(in_2), .SP_plus_plus(SP_plus_plus), .SP_minus_minus(SP_minus_minus));
  Register #(.width(1)) register_1 (.D(alu_1_out_4), .en(ZFLD), .Q(ZF), .clk(in_2));  // open: clr
  Multiplexer #(.select(3), .width(16)) multiplexer_4 (
    .in0(registerbank_1_dout0), .in1(registerbank_1_dout1), .in2(registerbank_1_dout2),
    .in3(registerbank_1_dout3), .in4(registerbank_1_dout4), .in5(registerbank_1_dout5),
    .in6(registerbank_1_dout6), .in7(registerbank_1_dout7), .out(Dout_t), .sel(ALU_OP[2:0]), .en(undriven));
  ALU alu_1 (
    .Din_1(Dout_t), .Din_2({multiplexer_6_out, MEM_ADDRESS}), .out_4(alu_1_out_4), .result(alu_1_result),
    .ALUOP(ALU_OP));
  Multiplexer #(.width(16)) multiplexer_5 (.in0(alu_1_result), .in1(Din), .out(DATA_IN), .sel(MUX));  // open: en
  Multiplexer #(.select(3), .width(16)) multiplexer_6 (
    .in0(registerbank_1_dout0), .in1(registerbank_1_dout1), .in2(registerbank_1_dout2),
    .in3(registerbank_1_dout3), .in4(registerbank_1_dout4), .in5(registerbank_1_dout5),
    .in6(registerbank_1_dout6), .in7(registerbank_1_dout7), .out({multiplexer_6_out, MEM_ADDRESS}),
    .sel(offset[5:3]));  // open: en
  ControlUnit controlunit_1 (
    .clk(in_2), .PCLD(PCLD), .PCINC(PCINC), .ARMUX2(ARMUX2), .REGLD(REGLD), .ZFLD(ZFLD), .MUX(MUX),
    .MEMLD(MEMLD), .adress(Din[15:12]), .ZF(ZF), .ARMUX1(ARMUX1), .SP_minus_minus(SP_minus_minus),
    .SP_plus_plus(SP_plus_plus), .DataMux(DataMux), .PCMux(PCMux), .IRLD(IRLD));
  Register #(.width(12)) register_2 (.D(Din[11:0]), .en(IRLD), .Q({ALU_OP, offset}), .clk(in_2));  // open: clr

  // Other names for the same wires on the sheet: CLK = in_2; R1[2:0] = offset[2:0]; R3[2:0] = offset[5:3];
  //   offset[11:6] = ALU_OP; R2[2:0] = ALU_OP[2:0]; PARTIAL_INSTRUCTION[11:0] = Din[11:0];
  //   WHOLE_INSTRUCTION[15:0] = Din; opcode[3:0] = Din[15:12]
endmodule

module ALU (
  input  [15:0] Din_1,
  input  [15:0] Din_2,
  input  [5:0] ALUOP,
  output out_4,
  output [15:0] result
);

  wire [15:0] adder_1_out, adder_2_out, and_1_out, multiplexer_1_out, not_1_out, or_1_out, subtractor_1_out,
       subtractor_2_out, xor_1_out;

  Adder #(.width(16)) adder_1 (.a(Din_2), .b(16'h1), .out(adder_1_out));  // open: cin, cout
  Subtractor #(.width(16)) subtractor_1 (.a(Din_2), .b(16'h1), .out(subtractor_1_out));  // open: bin, bout
  Adder #(.width(16)) adder_2 (.a(Din_1), .b(Din_2), .out(adder_2_out));  // open: cin, cout
  Subtractor #(.width(16)) subtractor_2 (.a(Din_1), .b(Din_2), .out(subtractor_2_out));  // open: bin, bout
  assign and_1_out = Din_1 & Din_2;  // AND_Gate and_1, 16 bits wide
  assign or_1_out = Din_1 | Din_2;  // OR_Gate or_1, 16 bits wide
  assign xor_1_out = Din_1 ^ Din_2;  // XOR_Gate xor_1, 16 bits wide
  assign not_1_out = ~Din_2;  // NOT_Gate not_1, 16 bits wide
  Multiplexer #(.select(3), .width(16)) multiplexer_1 (
    .in0(not_1_out), .in1(Din_2), .in2(adder_1_out), .in3(subtractor_1_out), .out(multiplexer_1_out),
    .sel(ALUOP[2:0]));  // open: in4, in5, in6, in7, en
  Multiplexer #(.select(3), .width(16)) multiplexer_2 (
    .in0(adder_2_out), .in1(subtractor_2_out), .in2(and_1_out), .in3(or_1_out), .in4(xor_1_out),
    .in7(multiplexer_1_out), .out(result), .sel(ALUOP[5:3]));  // open: in5, in6, en
  nor zf (out_4, result[0], result[1], result[2], result[3], result[4], result[5], result[6], result[7], result[8], result[9], result[10], result[11], result[12], result[13], result[14], result[15]);
endmodule

// Register Bank
module RegisterBank (
  input  [2:0] Reg_Select,
  input  REG_LOAD,
  input  [15:0] DATA_IN,
  input  Clock,
  input  SP_minus_minus,
  input  SP_plus_plus,
  output [15:0] DOUT0,
  output [15:0] DOUT1,
  output [15:0] DOUT2,
  output [15:0] DOUT3,
  output [15:0] DOUT4,
  output [15:0] DOUT5,
  output [15:0] DOUT6,
  output [15:0] DOUT7
);

  wire and_1_out, and_2_out, and_3_out, and_4_out, and_5_out, and_6_out, and_7_out, and_8_out,
       decoder_1_out0, decoder_1_out1, decoder_1_out2, decoder_1_out3, decoder_1_out4, decoder_1_out5,
       decoder_1_out6, or_1_out;
  wire [15:0] adder_1_out, multiplexer_1_out;

  Decoder #(.select(3), .enable("false")) decoder_1 (
    .out0(decoder_1_out0), .out1(decoder_1_out1), .out2(decoder_1_out2), .out3(decoder_1_out3),
    .out4(decoder_1_out4), .out5(decoder_1_out5), .out6(decoder_1_out6), .sel(Reg_Select));  // open: out7
  and and_1 (and_1_out, decoder_1_out0, REG_LOAD);
  and and_2 (and_2_out, decoder_1_out1, REG_LOAD);
  and and_3 (and_3_out, decoder_1_out2, REG_LOAD);
  and and_4 (and_4_out, decoder_1_out3, REG_LOAD);
  and and_5 (and_5_out, decoder_1_out4, REG_LOAD);
  and and_6 (and_6_out, decoder_1_out5, REG_LOAD);
  and and_7 (and_7_out, decoder_1_out6, REG_LOAD);
  Register #(.width(16)) register_1 (.D(DATA_IN), .en(and_1_out), .Q(DOUT0), .clk(Clock));  // open: clr
  Register #(.width(16)) register_2 (.D(DATA_IN), .en(and_2_out), .Q(DOUT1), .clk(Clock));  // open: clr
  Register #(.width(16)) register_3 (.D(DATA_IN), .en(and_3_out), .Q(DOUT2), .clk(Clock));  // open: clr
  Register #(.width(16)) register_4 (.D(DATA_IN), .en(and_4_out), .Q(DOUT3), .clk(Clock));  // open: clr
  Register #(.width(16)) register_5 (.D(DATA_IN), .en(and_5_out), .Q(DOUT4), .clk(Clock));  // open: clr
  Register #(.width(16)) register_6 (.D(DATA_IN), .en(and_6_out), .Q(DOUT5), .clk(Clock));  // open: clr
  Register #(.width(16)) register_7 (.D(DATA_IN), .en(and_7_out), .Q(DOUT6), .clk(Clock));  // open: clr
  Adder #(.width(16)) adder_1 (.a(DOUT7), .b(multiplexer_1_out), .out(adder_1_out));  // open: cin, cout
  Register #(.width(16)) register_8 (.D(adder_1_out), .en(or_1_out), .Q(DOUT7), .clk(Clock));  // open: clr
  or or_1 (or_1_out, SP_plus_plus, SP_minus_minus);
  Multiplexer #(.width(16)) multiplexer_1 (
    .in0({16{1'b1}}), .in1(16'h1), .out(multiplexer_1_out), .sel(and_8_out));  // open: en
  and and_8 (and_8_out, SP_plus_plus, ~SP_minus_minus);  // AND_Gate
endmodule

// CU
module ControlUnit (
  input  [3:0] adress,
  input  ZF,
  input  clk,
  output ARMUX2,
  output SP_minus_minus,
  output SP_plus_plus,
  output DataMux,
  output PCMux,
  output IRLD,
  output MEMLD,
  output MUX,
  output ZFLD,
  output REGLD,
  output ARMUX1,
  output PCINC,
  output PCLD
);

  wire Fetch, nAddr0, nAddr1, nAddr2, nAddr3;
  wire [1:1] and_1_out;
  wire [3:0] multiplexer_1_out, multiplexer_2_out, register_1_q;

  and and_1 (and_1_out[1], ~adress[0], ~adress[1], adress[2], ~adress[3]);  // AND_Gate
  Multiplexer #(.select(2), .width(4)) multiplexer_1 (
    .in0(adress), .in1(adress), .in2(4'b0000), .in3(4'b0101), .out(multiplexer_1_out),
    .sel({and_1_out[1], ZF}));  // open: en
  Multiplexer #(.width(4)) multiplexer_2 (
    .in0({nAddr3, nAddr2, nAddr1, nAddr0}), .in1(multiplexer_1_out), .out(multiplexer_2_out), .sel(Fetch));  // open: en
  Register #(.width(4)) register_1 (.D(multiplexer_2_out), .en(1'b1), .Q(register_1_q), .clk(clk));  // open: clr
  ROM #(.addrWidth(4), .dataWidth(18)) rom_1 (
    .addr(register_1_q),
    .data({Fetch, PCLD, PCINC, ARMUX1, REGLD, ZFLD, MUX, MEMLD, IRLD, PCMux, DataMux, SP_plus_plus, SP_minus_minus, nAddr3, nAddr2, nAddr1, nAddr0, ARMUX2}));  // open: sel

  // Notes on the sheet:
  //   contents of rom_1 (hex, n*v repeats v):
  //   141 54 34 22 0 80 0 18
endmodule

module Main (
  input  [15:0] Switch2,
  input  [15:0] Switch1
);

  wire CLK, MEMLD, memwt, PB1_Selector, PB2_Selector, S1_Selector, S2_Selector;
  wire [11:0] Addr;
  wire [15:0] BirdDout, Memdout, undriven;

  and and_1 (MEMLD, ~Addr[11], memwt);  // AND_Gate
  Clock clock_1 (.out(CLK));
  RAM #(.addrWidth(12), .dataWidth(16), .bus("separate")) ram_1 (
    .addr(Addr), .din(BirdDout), .data(Memdout), .str(MEMLD), .clk(CLK));  // open: sel, ld, clr
  and S1 (S1_Selector, Addr[0], Addr[1], Addr[2], Addr[3], Addr[4], Addr[5], Addr[6], Addr[7], ~Addr[8], ~Addr[9], ~Addr[10], ~Addr[11]);  // AND_Gate
  and PB1 (PB1_Selector, Addr[0], Addr[1], Addr[2], Addr[3], Addr[4], Addr[5], Addr[6], Addr[7], ~Addr[8], ~Addr[9], Addr[10], Addr[11]);  // AND_Gate
  and S2 (S2_Selector, Addr[0], Addr[1], Addr[2], Addr[3], Addr[4], Addr[5], Addr[6], Addr[7], ~Addr[8], ~Addr[9], ~Addr[10], Addr[11]);  // AND_Gate
  and PB2 (PB2_Selector, Addr[0], Addr[1], Addr[2], Addr[3], Addr[4], Addr[5], Addr[6], Addr[7], ~Addr[8], ~Addr[9], Addr[10], ~Addr[11]);  // AND_Gate
  Hex_Digit_Display hex_digit_display_1 (.value(undriven[15:12]));  // open: dp
  Hex_Digit_Display hex_digit_display_2 (.value(undriven[7:4]));  // open: dp
  Hex_Digit_Display hex_digit_display_3 (.value(undriven[11:8]));  // open: dp
  Hex_Digit_Display hex_digit_display_4 (.value(undriven[3:0]));  // open: dp

  // Other names for the same wires on the sheet: S1Dout[15:0] = Switch1; S2Dout[15:0] = Switch2
endmodule
