// Logisim project logisim.circ as structural Verilog: 11 circuits, main circuit main_ver
// Register Bank
module register_bank (
  input  [2:0] Reg_select,
  input  Reg_load,
  input  clock,
  input  [15:0] Data_in,
  input  sp_plus_plus,
  input  sp_minus_minus,
  output [15:0] dout0,
  output [15:0] dout1,
  output [15:0] dout2,
  output [15:0] dout3,
  output [15:0] dout4,
  output [15:0] dout5,
  output [15:0] dout6,
  output [15:0] dout7
);

  wire and_1_out, and_2_out, and_3_out, and_4_out, and_5_out, and_6_out, and_7_out, and_8_out, and_9_out,
       decoder_1_out0, decoder_1_out1, decoder_1_out2, decoder_1_out3, decoder_1_out4, decoder_1_out5,
       decoder_1_out6, decoder_1_out7, or_1_out;
  wire [15:0] adder_1_out, multiplexer_1_out;

  Decoder #(.select(3), .enable("false")) decoder_1 (
    .out0(decoder_1_out0), .out1(decoder_1_out1), .out2(decoder_1_out2), .out3(decoder_1_out3),
    .out4(decoder_1_out4), .out5(decoder_1_out5), .out6(decoder_1_out6), .out7(decoder_1_out7),
    .sel(Reg_select));
  and and_1 (and_1_out, decoder_1_out0, Reg_load);
  and and_2 (and_2_out, decoder_1_out1, Reg_load);
  and and_3 (and_3_out, decoder_1_out2, Reg_load);
  and and_4 (and_4_out, decoder_1_out3, Reg_load);
  and and_5 (and_5_out, decoder_1_out4, Reg_load);
  and and_6 (and_6_out, decoder_1_out5, Reg_load);
  and and_7 (and_7_out, decoder_1_out6, Reg_load);
  and and_8 (and_8_out, decoder_1_out7, Reg_load);
  Register #(.width(16)) register_1 (.D(Data_in), .en(and_1_out), .Q(dout0), .clk(clock));  // open: clr
  Register #(.width(16)) register_2 (.D(Data_in), .en(and_2_out), .Q(dout1), .clk(clock));  // open: clr
  Register #(.width(16)) register_3 (.D(Data_in), .en(and_3_out), .Q(dout2), .clk(clock));  // open: clr
  Register #(.width(16)) register_4 (.D(Data_in), .en(and_4_out), .Q(dout3), .clk(clock));  // open: clr
  Register #(.width(16)) register_5 (.D(Data_in), .en(and_5_out), .Q(dout4), .clk(clock));  // open: clr
  Register #(.width(16)) register_6 (.D(Data_in), .en(and_6_out), .Q(dout5), .clk(clock));  // open: clr
  Register #(.width(16)) register_7 (.D(Data_in), .en(and_7_out), .Q(dout6), .clk(clock));  // open: clr
  Register #(.width(16)) register_8 (.D(Data_in), .en(and_8_out), .clk(clock));  // open: Q, clr
  Adder #(.width(16)) adder_1 (.a(dout7), .b(multiplexer_1_out), .out(adder_1_out));  // open: cin, cout
  Register #(.width(16)) register_9 (.D(adder_1_out), .en(or_1_out), .Q(dout7), .clk(clock));  // open: clr
  or or_1 (or_1_out, sp_plus_plus, sp_minus_minus);
  and and_9 (and_9_out, ~sp_minus_minus, sp_plus_plus);  // AND_Gate
  Multiplexer #(.width(16), .enable("false")) multiplexer_1 (
    .in0({16{1'b1}}), .in1(16'h1), .out(multiplexer_1_out), .sel(and_9_out));
endmodule

// ALU
module reptile_8_ALU (
  input  [15:0] Din1,
  input  [15:0] Din2,
  input  [5:0] ALUOP,
  output Z,
  output [15:0] result
);

  wire [15:0] adder_1_out, adder_2_out, and_1_out, multiplexer_1_out, not_1_out, or_1_out, subtractor_1_out,
       subtractor_2_out, xor_1_out;

  Adder #(.width(16)) adder_1 (.a(Din1), .b(Din2), .out(adder_1_out));  // open: cin, cout
  Subtractor #(.width(16)) subtractor_1 (.a(Din1), .b(Din2), .out(subtractor_1_out));  // open: bin, bout
  assign and_1_out = Din1 & Din2;  // AND_Gate and_1, 16 bits wide
  assign or_1_out = Din1 | Din2;  // OR_Gate or_1, 16 bits wide
  assign xor_1_out = Din1 ^ Din2;  // XOR_Gate xor_1, 16 bits wide
  assign not_1_out = ~Din2;  // NOT_Gate not_1, 16 bits wide
  Adder #(.width(16)) adder_2 (.a(Din2), .b(16'h1), .out(adder_2_out));  // open: cin, cout
  Subtractor #(.width(16)) subtractor_2 (.a(Din2), .b(16'h1), .out(subtractor_2_out));  // open: bin, bout
  Multiplexer #(.select(3), .width(16)) multiplexer_1 (
    .in0(not_1_out), .in1(Din2), .in2(adder_2_out), .in3(subtractor_2_out), .out(multiplexer_1_out),
    .sel(ALUOP[2:0]));  // open: in4, in5, in6, in7, en
  Multiplexer #(.select(3), .width(16)) multiplexer_2 (
    .in0(adder_1_out), .in1(subtractor_1_out), .in2(and_1_out), .in3(or_1_out), .in4(xor_1_out),
    .in7(multiplexer_1_out), .out(result), .sel(ALUOP[5:3]));  // open: in5, in6, en
  nor zf (Z, result[0], result[1], result[2], result[3], result[4], result[5], result[6], result[7], result[8], result[9], result[10], result[11], result[12], result[13], result[14], result[15]);
endmodule

// Control Unit
module control_unit_bird (
  input  [3:0] opcode,
  input  ZF,
  input  clock,
  output IRLD,
  output MEMLD,
  output MUX,
  output ZFLD,
  output REGLD,
  output ARMUXBit0,
  output ARMUXBit1,
  output PCINC,
  output PCLD,
  output SP_minus_minus,
  output SP_plus_plus,
  output PCMUX,
  output DataMux
);

  wire fetch, nextAddr0, nextAddr1, nextAddr2, nextAddr3;
  wire [1:1] and_1_out;
  wire [3:0] multiplexer_1_out, multiplexer_2_out, register_1_q;

  and and_1 (and_1_out[1], ~opcode[0], ~opcode[1], opcode[2], ~opcode[3]);  // AND_Gate
  Multiplexer #(.select(2), .width(4)) multiplexer_1 (
    .in0(opcode), .in1(opcode), .in2(4'b0000), .in3(4'b0101), .out(multiplexer_1_out),
    .sel({and_1_out[1], ZF}));  // open: en
  Multiplexer #(.width(4)) multiplexer_2 (
    .in0({nextAddr3, nextAddr2, nextAddr1, nextAddr0}), .in1(multiplexer_1_out), .out(multiplexer_2_out),
    .sel(fetch));  // open: en
  Register #(.width(4)) register_1 (.D(multiplexer_2_out), .Q(register_1_q), .clk(clock));  // open: en, clr
  ROM #(.addrWidth(4), .dataWidth(18)) rom_1 (
    .addr(register_1_q),
    .data({fetch, DataMux, PCMUX, SP_plus_plus, SP_minus_minus, PCLD, PCINC, ARMUXBit1, ARMUXBit0, REGLD, ZFLD, MUX, MEMLD, IRLD, nextAddr3, nextAddr2, nextAddr1, nextAddr0}));  // open: sel

  // Notes on the sheet:
  //   contents of rom_1 (hex, n*v repeats v):
  //   20810 940 340 220 0 1000 0 180 2420 400c 13420 400d 540 9400
endmodule

// Bird
module bird (
  input  [15:0] Din,
  input  clock,
  output [15:0] Dout,
  output memwt,
  output [15:0] Addr
);

  wire ARMUXbit0, ARMUXbit1, DataMux, IRLD, MUX, PCINC, PCLD, PCMUX, REGLD, reptile_8_alu_1_z,
       SP_minus_minus, SP_plus_plus, zf, ZFLD;
  wire [5:0] AluOp, offset;
  wire [11:0] negator_1_out;
  wire [15:0] adder_1_out, Data_in, Dout_t, mem_addr, multiplexer_1_out, multiplexer_3_out, PCValue,
       register_bank_1_dout0, register_bank_1_dout1, register_bank_1_dout2, register_bank_1_dout3,
       register_bank_1_dout4, register_bank_1_dout5, register_bank_1_dout6, reptile_8_alu_1_result, SP,
       subtractor_1_out;

  Multiplexer #(.width(16)) multiplexer_1 (
    .in0(multiplexer_3_out), .in1(Din), .out(multiplexer_1_out), .sel(PCMUX));  // open: en
  Counter #(.width(16), .max('hffff)) counter_1 (
    .load(PCLD), .D(multiplexer_1_out), .count(PCINC), .Q(PCValue), .clk(clock));  // open: carry, clr
  Adder #(.width(16)) adder_1 (.a(PCValue), .b({4'b0000, AluOp, offset}), .out(adder_1_out));  // open: cin, cout
  Subtractor #(.width(16)) subtractor_1 (
    .a(PCValue), .b({4'b0000, negator_1_out}), .out(subtractor_1_out));  // open: bin, bout
  Negator #(.width(12)) negator_1 (.in({AluOp, offset}), .out(negator_1_out));
  Multiplexer #(.width(16), .enable("false")) multiplexer_2 (.in0(Dout_t), .in1(PCValue), .out(Dout), .sel(DataMux));
  Multiplexer #(.width(16), .enable("false")) multiplexer_3 (
    .in0(adder_1_out), .in1(subtractor_1_out), .out(multiplexer_3_out), .sel(AluOp[5]));
  Multiplexer #(.select(2), .width(16)) multiplexer_4 (
    .in0(PCValue), .in1(mem_addr), .in2(SP), .out(Addr), .sel({ARMUXbit1, ARMUXbit0}));  // open: in3, en
  register_bank register_bank_1 (
    .Reg_select(offset[2:0]), .Reg_load(REGLD), .Data_in(Data_in), .dout0(register_bank_1_dout0),
    .dout1(register_bank_1_dout1), .dout2(register_bank_1_dout2), .dout3(register_bank_1_dout3),
    .dout4(register_bank_1_dout4), .dout5(register_bank_1_dout5), .dout6(register_bank_1_dout6), .dout7(SP),
    .clock(clock), .sp_plus_plus(SP_plus_plus), .sp_minus_minus(SP_minus_minus));
  Register #(.width(1)) register_1 (.D(reptile_8_alu_1_z), .en(ZFLD), .Q(zf), .clk(clock));  // open: clr
  Multiplexer #(.select(3), .width(16)) multiplexer_5 (
    .in0(register_bank_1_dout0), .in1(register_bank_1_dout1), .in2(register_bank_1_dout2),
    .in3(register_bank_1_dout3), .in4(register_bank_1_dout4), .in5(register_bank_1_dout5),
    .in6(register_bank_1_dout6), .in7(SP), .out(Dout_t), .sel(AluOp[2:0]));  // open: en
  reptile_8_ALU reptile_8_alu_1 (
    .Din1(Dout_t), .Din2(mem_addr), .Z(reptile_8_alu_1_z), .result(reptile_8_alu_1_result), .ALUOP(AluOp));
  Multiplexer #(.width(16)) multiplexer_6 (
    .in0(reptile_8_alu_1_result), .in1(Din), .out(Data_in), .sel(MUX));  // open: en
  Multiplexer #(.select(3), .width(16)) multiplexer_7 (
    .in0(register_bank_1_dout0), .in1(register_bank_1_dout1), .in2(register_bank_1_dout2),
    .in3(register_bank_1_dout3), .in4(register_bank_1_dout4), .in5(register_bank_1_dout5),
    .in6(register_bank_1_dout6), .in7(SP), .out(mem_addr), .sel(offset[5:3]));  // open: en
  control_unit_bird control_unit_bird_1 (
    .SP_minus_minus(SP_minus_minus), .SP_plus_plus(SP_plus_plus), .DataMux(DataMux), .PCMUX(PCMUX),
    .PCLD(PCLD), .ARMUXBit0(ARMUXbit0), .REGLD(REGLD), .MEMLD(memwt), .ZFLD(ZFLD), .opcode(Din[15:12]),
    .ARMUXBit1(ARMUXbit1), .ZF(zf), .clock(clock), .IRLD(IRLD), .PCINC(PCINC), .MUX(MUX));
  Register #(.width(12)) register_2 (.D(Din[11:0]), .en(IRLD), .Q({AluOp, offset}), .clk(clock));  // open: clr

  // Other names for the same wires on the sheet: clk = clock; MEMLD = memwt; r1[2:0] = offset[2:0];
  //   r3[2:0] = offset[5:3]; offset[11:6] = AluOp; r2[2:0] = AluOp[2:0]; partial_instruction[11:0] = Din[11:0];
  //   whole_instruction[15:0] = Din; opcode[3:0] = Din[15:12]
endmodule

module main (
  input  [15:0] SB2,
  input  [15:0] SB1
);

  wire and_1_out, and_2_out, and_3_out, and_4_out, and_6_out, clk, MEMLD, memwt, pb1_2_out, pb1_selector,
       pb2_2_out, pb2_selector, s1_selector, s2_selector, sseg_selector;
  wire [0:0] pb1Dout, pb2Dout;
  wire [3:0] register_3_q_2;
  wire [11:0] register_3_q;
  wire [15:0] Addr, birdDout, Memdout, multiplexer_1_out, multiplexer_2_out, multiplexer_3_out,
       multiplexer_4_out, multiplexer_5_out;

  and s2 (s2_selector, Addr[15], Addr[14], Addr[13], Addr[12], Addr[11], Addr[10], Addr[9], Addr[8], Addr[7], Addr[6], Addr[5], Addr[4], ~Addr[3], ~Addr[2], ~Addr[1], Addr[0]);  // AND_Gate
  and pb2 (pb2_selector, Addr[15], Addr[14], Addr[13], Addr[12], Addr[11], Addr[10], Addr[9], Addr[8], Addr[7], Addr[6], Addr[5], Addr[4], ~Addr[3], ~Addr[2], Addr[1], Addr[0]);  // AND_Gate
  Button pb2_2 (.out(pb2_2_out));
  Register #(.width(1)) register_1 (.D(and_1_out), .en(and_1_out), .Q(pb2Dout[0]), .clk(clk), .clr(and_2_out));
  and and_1 (and_1_out, ~pb2Dout[0], pb2_2_out);  // AND_Gate
  and and_2 (and_2_out, sseg_selector, pb2Dout[0]);
  and s1 (s1_selector, Addr[15], Addr[14], Addr[13], Addr[12], Addr[11], Addr[10], Addr[9], Addr[8], Addr[7], Addr[6], Addr[5], Addr[4], ~Addr[3], ~Addr[2], ~Addr[1], ~Addr[0]);  // AND_Gate
  and pb1 (pb1_selector, Addr[15], Addr[14], Addr[13], Addr[12], Addr[11], Addr[10], Addr[9], Addr[8], Addr[7], Addr[6], Addr[5], Addr[4], ~Addr[3], ~Addr[2], Addr[1], ~Addr[0]);  // AND_Gate
  Button pb1_2 (.out(pb1_2_out));
  Register #(.width(1)) register_2 (.D(and_3_out), .en(and_3_out), .Q(pb1Dout[0]), .clk(clk), .clr(and_4_out));
  and and_3 (and_3_out, ~pb1Dout[0], pb1_2_out);  // AND_Gate
  Clock clock_1 (.out(clk));
  and and_4 (and_4_out, sseg_selector, pb1Dout[0]);
  Multiplexer #(.width(16), .enable("false")) multiplexer_1 (
    .in0({16{1'b0}}), .in1({{15{1'b0}}, pb2Dout[0]}), .out(multiplexer_1_out), .sel(pb2_selector));
  Multiplexer #(.width(16), .enable("false")) multiplexer_2 (
    .in0(multiplexer_1_out), .in1({{15{1'b0}}, pb1Dout[0]}), .out(multiplexer_2_out), .sel(pb1_selector));
  Multiplexer #(.width(16), .enable("false")) multiplexer_3 (
    .in0(multiplexer_2_out), .in1(SB2), .out(multiplexer_3_out), .sel(s2_selector));
  and and_5 (MEMLD, ~Addr[15], memwt);  // AND_Gate
  RAM #(.addrWidth(16), .dataWidth(16), .bus("separate")) ram_1 (
    .addr(Addr), .din(birdDout), .data(Memdout), .str(MEMLD), .clk(clk));  // open: sel, ld, clr
  Multiplexer #(.width(16), .enable("false")) multiplexer_4 (
    .in0(multiplexer_3_out), .in1(SB1), .out(multiplexer_4_out), .sel(s1_selector));
  Multiplexer #(.width(16), .enable("false")) multiplexer_5 (
    .in0(Memdout), .in1(multiplexer_4_out), .out(multiplexer_5_out), .sel(Addr[15]));
  bird bird_1 (.Dout(birdDout), .Addr(Addr), .memwt(memwt), .Din(multiplexer_5_out), .clock(clk));
  and and_6 (and_6_out, sseg_selector, memwt);
  Hex_Digit_Display hex_digit_display_1 (.value(register_3_q_2));  // open: dp
  Hex_Digit_Display hex_digit_display_2 (.value(register_3_q[11:8]));  // open: dp
  Register #(.width(16)) register_3 (
    .D(birdDout), .en(and_6_out), .Q({register_3_q_2, register_3_q}), .clk(clk));  // open: clr
  and sseg (sseg_selector, Addr[15], Addr[14], Addr[13], Addr[12], Addr[11], Addr[10], Addr[9], Addr[8], Addr[7], Addr[6], Addr[5], Addr[4], ~Addr[3], Addr[2], ~Addr[1], ~Addr[0]);  // AND_Gate
  Hex_Digit_Display hex_digit_display_3 (.value(register_3_q[3:0]));  // open: dp
  Hex_Digit_Display hex_digit_display_4 (.value(register_3_q[7:4]));  // open: dp

  // Other names for the same wires on the sheet: s1Dout[15:0] = SB1; s2Dout[15:0] = SB2
endmodule

// Control Unit
module control_unit_vertebrate (
  input  [3:0] opcode,
  input  ZF,
  input  INT,
  input  IF,
  input  clock,
  output IRLD,
  output MEMLD,
  output MUX,
  output ZFLD,
  output REGLD,
  output ARMUXBit0,
  output ARMUXBit1,
  output PCINC,
  output PCLD,
  output SP_minus_minus,
  output SP_plus_plus,
  output PCMUX,
  output DataMux0,
  output DataMux1,
  output FLAGWT,
  output INTACK,
  output INTLD,
  output STI,
  output CLI
);

  wire and_2_out, fetch, nand_1_out, nextAddr0, nextAddr1, nextAddr2, nextAddr3, nextAddr4;
  wire [1:1] and_1_out;
  wire [3:0] multiplexer_1_out;
  wire [4:0] multiplexer_2_out, multiplexer_3_out, register_1_q;

  and and_1 (and_1_out[1], ~opcode[0], ~opcode[1], opcode[2], ~opcode[3]);  // AND_Gate
  Multiplexer #(.select(2), .width(4)) multiplexer_1 (
    .in0(opcode), .in1(opcode), .in2(4'b0000), .in3(4'b0101), .out(multiplexer_1_out),
    .sel({and_1_out[1], ZF}));  // open: en
  nand nand_1 (nand_1_out, nextAddr0, nextAddr1, nextAddr2, nextAddr3, nextAddr4);
  and and_2 (and_2_out, IF, INT, nand_1_out);
  Multiplexer #(.width(5)) multiplexer_2 (
    .in0({nextAddr4, nextAddr3, nextAddr2, nextAddr1, nextAddr0}), .in1({1'b0, multiplexer_1_out}),
    .out(multiplexer_2_out), .sel(fetch));  // open: en
  Register #(.width(5)) register_1 (.D(multiplexer_3_out), .en(1'b1), .Q(register_1_q), .clk(clock));  // open: clr
  Multiplexer #(.width(5)) multiplexer_3 (
    .in0(multiplexer_2_out), .in1(5'b10100), .out(multiplexer_3_out), .sel(and_2_out));  // open: en
  ROM #(.addrWidth(5), .dataWidth(25)) rom_1 (
    .addr(register_1_q),
    .data({CLI, STI, INTLD, INTACK, FLAGWT, fetch, DataMux1, DataMux0, PCMUX, SP_plus_plus, SP_minus_minus, PCLD, PCINC, ARMUXBit1, ARMUXBit0, REGLD, ZFLD, MUX, MEMLD, IRLD, nextAddr4, nextAddr3, nextAddr2, nextAddr1, nextAddr0}));  // open: sel

  // Notes on the sheet:
  //   contents of rom_1 (hex, n*v repeats v):
  //   81020 1280 680 440 0 38 0 300 4840 8012 4857 8013 800000 1000000 8010 0 108811 12800 a80 12800
  //   1024855 664856 812c00 12000 2000
endmodule

// Register Bank
module register_bank_vertebrate (
  input  [2:0] Reg_select,
  input  CLI,
  input  Z,
  input  ZFSET,
  input  STI,
  input  Reg_load,
  input  FLAGWT,
  input  [15:0] Data_in,
  input  clock,
  input  sp_plus_plus,
  input  sp_minus_minus,
  output [15:0] dout0,
  output [15:0] dout1,
  output [15:0] dout2,
  output [15:0] dout3,
  output [15:0] dout4,
  output [15:0] dout5,
  output ZF,
  output IF,
  output [15:0] dout7
);

  wire and_1_out, and_2_out, and_3_out, and_4_out, and_5_out, and_6_out, and_9_out, and_10_out, and_11_out,
       and_12_out, and_13_out, decoder_1_out0, decoder_1_out1, decoder_1_out2, decoder_1_out3,
       decoder_1_out4, decoder_1_out5, decoder_1_out6, decoder_1_out7, or_1_out, or_2_out, or_3_out,
       or_4_out, or_5_out, or_6_out, or_7_out, reg7ld;
  wire [15:0] adder_1_out, multiplexer_1_out, StackValue, subtractor_1_out;

  Decoder #(.select(3), .enable("false")) decoder_1 (
    .out0(decoder_1_out0), .out1(decoder_1_out1), .out2(decoder_1_out2), .out3(decoder_1_out3),
    .out4(decoder_1_out4), .out5(decoder_1_out5), .out6(decoder_1_out6), .out7(decoder_1_out7),
    .sel(Reg_select));
  and and_1 (and_1_out, decoder_1_out0, Reg_load);
  and and_2 (and_2_out, decoder_1_out1, Reg_load);
  and and_3 (and_3_out, decoder_1_out2, Reg_load);
  and and_4 (and_4_out, decoder_1_out3, Reg_load);
  and and_5 (and_5_out, decoder_1_out4, Reg_load);
  and and_6 (and_6_out, decoder_1_out5, Reg_load);
  // AND_Gate and_7 has open pins: in1=decoder_1_out6, in3=Reg_load, out=open
  and and_8 (reg7ld, decoder_1_out7, Reg_load);
  Register #(.width(16)) register_1 (.D(Data_in), .en(and_1_out), .Q(dout0), .clk(clock));  // open: clr
  Register #(.width(16)) register_2 (.D(Data_in), .en(and_2_out), .Q(dout1), .clk(clock));  // open: clr
  Register #(.width(16)) register_3 (.D(Data_in), .en(and_3_out), .Q(dout2), .clk(clock));  // open: clr
  Register #(.width(16)) register_4 (.D(Data_in), .en(and_4_out), .Q(dout3), .clk(clock));  // open: clr
  Register #(.width(16)) register_5 (.D(Data_in), .en(and_5_out), .Q(dout4), .clk(clock));  // open: clr
  Register #(.width(16)) register_6 (.D(Data_in), .en(and_6_out), .Q(dout5), .clk(clock));  // open: clr
  Multiplexer #(.width(16)) multiplexer_1 (
    .in0(Data_in), .in1(StackValue), .out(multiplexer_1_out), .sel(or_1_out));  // open: en
  or or_1 (or_1_out, sp_plus_plus, sp_minus_minus);
  and and_9 (and_9_out, Data_in[0], FLAGWT);
  and and_10 (and_10_out, ~Data_in[0], FLAGWT);  // AND_Gate
  or or_2 (or_2_out, CLI, and_9_out);
  or or_3 (or_3_out, STI, and_10_out);
  Register #(.width(16)) register_7 (.D(multiplexer_1_out), .en(or_4_out), .Q(dout7), .clk(clock));  // open: clr
  or or_4 (or_4_out, sp_plus_plus, sp_minus_minus, reg7ld);
  S_R_Flip_Flop s_r_ff_1 (.S(or_3_out), .clk(clock), .R(or_2_out), .Q(IF));  // open: Qn, preset, reset, en
  and and_11 (and_11_out, Data_in[0], FLAGWT);
  and and_12 (and_12_out, ~Data_in[0], FLAGWT);  // AND_Gate
  Adder #(.width(16)) adder_1 (.a(dout7), .b(16'h1), .out(adder_1_out));  // open: cin, cout
  Subtractor #(.width(16)) subtractor_1 (.a(dout7), .b(16'h1), .out(subtractor_1_out));  // open: bin, bout
  or or_5 (or_5_out, and_11_out, and_13_out);
  and and_13 (and_13_out, Z, ZFSET);
  or or_6 (or_6_out, and_12_out, or_7_out);
  or or_7 (or_7_out, ~Z, ZFSET);  // OR_Gate
  Multiplexer #(.width(16), .enable("false")) multiplexer_2 (
    .in0(adder_1_out), .in1(subtractor_1_out), .out(StackValue), .sel(sp_minus_minus));
  S_R_Flip_Flop s_r_ff_2 (.S(or_5_out), .clk(clock), .R(or_6_out), .Q(ZF));  // open: Qn, preset, reset, en
endmodule

// Vertebrate
module vertebrate (
  input  [15:0] Din,
  input  test,
  input  clock,
  output [15:0] Dout,
  output memwt,
  output [15:0] Addr,
  output INTACK,
  output [15:0] Vector
);

  wire ARMUXbit0, ARMUXbit1, CLI, DataMux0, DataMux1, DeviceTimer, FLAGWT, IF, INT, INTLD, IRLD, MUX, PCINC,
       PCLD, PCMUX, REGLD, SP_minus_minus, SP_plus_plus, STI, Z, ZF, ZFLD;
  wire [5:0] AluOp;
  wire [15:0] adder_1_out, adder_2_out, Data_in, Dout_t, ISR, mem_addr, multiplexer_1_out, multiplexer_3_out,
       negator_1_out, offset, PCValue, register_bank_vertebrate_1_p15, register_bank_vertebrate_1_p16,
       register_bank_vertebrate_1_p17, register_bank_vertebrate_1_p18, register_bank_vertebrate_1_p19,
       register_bank_vertebrate_1_p20, reptile_8_alu_1_result, SP, subtractor_1_out;

  // Probe on multiplexer_1_out
  Multiplexer #(.width(16)) multiplexer_1 (
    .in0(multiplexer_3_out), .in1(Din), .out(multiplexer_1_out), .sel(PCMUX));  // open: en
  // Probe on PCValue
  Counter #(.width(16), .max('hffff)) counter_1 (
    .load(PCLD), .D(multiplexer_1_out), .count(PCINC), .Q(PCValue), .clk(clock));  // open: carry, clr
  Adder #(.width(16)) adder_1 (
    .a(PCValue), .b({offset[15:12], AluOp, offset[5:0]}), .out(adder_1_out));  // open: cin, cout
  Subtractor #(.width(16)) subtractor_1 (.a(PCValue), .b(negator_1_out), .out(subtractor_1_out));  // open: bin, bout
  // Probe on negator_1_out
  Negator #(.width(16)) negator_1 (.in({offset[15:12], AluOp, offset[5:0]}), .out(negator_1_out));
  Multiplexer #(.select(2), .width(16), .enable("false")) multiplexer_2 (
    .in0(Dout_t), .in1(PCValue), .in2({{14{1'b0}}, IF, ZF}), .in3({16{1'b0}}), .out(Dout),
    .sel({DataMux1, DataMux0}));
  // Probe on multiplexer_3_out
  Multiplexer #(.width(16), .enable("false")) multiplexer_3 (
    .in0(adder_1_out), .in1(subtractor_1_out), .out(multiplexer_3_out), .sel(offset[15]));
  Multiplexer #(.select(2), .width(16)) multiplexer_4 (
    .in0(PCValue), .in1(mem_addr), .in2(SP), .in3(ISR), .out(Addr), .sel({ARMUXbit1, ARMUXbit0}));  // open: en
  // register_bank_vertebrate register_bank_vertebrate_1: pin names not known; wires that end beside it: CLI, Z, STI, REGLD, Data_in, FLAGWT, ZFLD, offset[2:0], SP_plus_plus, IF, IF, SP_minus_minus, ZF, clock, register_bank_vertebrate_1_p15, register_bank_vertebrate_1_p16, register_bank_vertebrate_1_p17, register_bank_vertebrate_1_p18, register_bank_vertebrate_1_p19, register_bank_vertebrate_1_p20, SP
  Multiplexer #(.select(3), .width(16)) multiplexer_5 (
    .in0(register_bank_vertebrate_1_p15), .in1(register_bank_vertebrate_1_p16),
    .in2(register_bank_vertebrate_1_p17), .in3(register_bank_vertebrate_1_p18),
    .in4(register_bank_vertebrate_1_p19), .in5(register_bank_vertebrate_1_p20), .in6({16{1'b0}}), .in7(SP),
    .out(Dout_t), .sel(AluOp[2:0]));  // open: en
  Adder #(.width(16)) adder_2 (.a(Din), .b(16'h7f0), .out(adder_2_out));  // open: cin, cout
  Timer timer_1 (.clk(clock), .DeviceTimer(DeviceTimer));  // open: out_3
  reptile_8_ALU reptile_8_alu_1 (.Din1(Dout_t), .Din2(mem_addr), .Z(Z), .result(reptile_8_alu_1_result), .ALUOP(AluOp));
  Multiplexer #(.width(16)) multiplexer_6 (
    .in0(reptile_8_alu_1_result), .in1(Din), .out(Data_in), .sel(MUX));  // open: en
  Register #(.width(16)) register_1 (.D(adder_2_out), .en(INTLD), .Q(ISR), .clk(clock));  // open: clr
  pic pic_1 (.INT(INT), .DeviceTimer(test), .Vector(Vector));
  Multiplexer #(.select(3), .width(16)) multiplexer_7 (
    .in0(register_bank_vertebrate_1_p15), .in1(register_bank_vertebrate_1_p16),
    .in2(register_bank_vertebrate_1_p17), .in3(register_bank_vertebrate_1_p18),
    .in4(register_bank_vertebrate_1_p19), .in5(register_bank_vertebrate_1_p20), .in6({16{1'b0}}), .in7(SP),
    .out(mem_addr), .sel(offset[5:3]));  // open: en
  // Probe on register_bank_vertebrate_1_p20
  // Probe on SP
  control_unit_vertebrate control_unit_vertebrate_1 (
    .INT(INT), .IRLD(IRLD), .MEMLD(memwt), .MUX(MUX), .ZFLD(ZFLD), .REGLD(REGLD), .ARMUXBit0(ARMUXbit0),
    .ARMUXBit1(ARMUXbit1), .PCINC(PCINC), .IF(IF), .PCLD(PCLD), .SP_minus_minus(SP_minus_minus),
    .SP_plus_plus(SP_plus_plus), .PCMUX(PCMUX), .DataMux0(DataMux0), .DataMux1(DataMux1), .FLAGWT(FLAGWT),
    .INTACK(INTACK), .INTLD(INTLD), .STI(STI), .CLI(CLI), .opcode(Din[15:12]), .ZF(ZF), .clock(clock));
  // Probe on Din
  Register #(.width(16)) register_2 (
    .D(Din), .en(IRLD), .Q({offset[15:12], AluOp, offset[5:0]}), .clk(clock));  // open: clr
  // Probe on {offset[15:12], AluOp, offset[5:0]}

  // Other names for the same wires on the sheet: clk = clock; MEMLD = memwt; r1[2:0] = offset[2:0];
  //   r3[2:0] = offset[5:3]; offset[11:6] = AluOp; r2[2:0] = AluOp[2:0]; whole_instruction[15:0] = Din;
  //   opcode[3:0] = Din[15:12]
endmodule

// PIC
module pic (
  input  DeviceTimer,
  output INT,
  output [15:0] Vector
);

  wire priority_encoder_1_en_out;

  not not_1 (INT, priority_encoder_1_en_out);
  Priority_Encoder priority_encoder_1 (
    .in0(DeviceTimer), .out(Vector[2:0]), .en_out(priority_encoder_1_en_out));  // open: in1, in2, in3, in4, in5, in6, in7, en_in, gs

  assign Vector[15:3] = {13{1'b0}};
endmodule

module Timer (
  input  clk,
  output DeviceTimer,
  output out_3
);

  wire [10:0] counter_1_q;
  wire [15:0] adder_1_out, register_1_q;

  Counter #(.width(11), .max('h7ff)) counter_1 (
    .load(1'b1), .D({11{1'b1}}), .count(1'b1), .Q(counter_1_q), .carry(out_3), .clk(clk), .clr(1'b0));
  and and_1 (DeviceTimer, counter_1_q[0], counter_1_q[1], counter_1_q[2], counter_1_q[3], counter_1_q[4], counter_1_q[5], counter_1_q[6], counter_1_q[7], counter_1_q[8], counter_1_q[9], counter_1_q[10]);
  // Probe on DeviceTimer
  Adder #(.width(16)) adder_1 (.a({{15{1'b0}}, DeviceTimer}), .b(register_1_q), .out(adder_1_out));  // open: cin, cout
  Register #(.width(16)) register_1 (.D(adder_1_out), .en(1'b1), .Q(register_1_q), .clk(clk));  // open: clr
endmodule

module main_ver (
  input  [15:0] SB2,
  input  [15:0] SB1,
  input  in_3
);

  wire and_1_out, and_2_out, and_3_out, and_4_out, and_6_out, and_7_out, clk, INTACK, MEMLD, memwt,
       pb1_2_out, pb1_selector, pb2_2_out, pb2_selector, s1_selector, s2_selector, sseg_selector,
       timer_selector;
  wire [0:0] pb1Dout, pb2Dout;
  wire [3:0] register_3_q_2, register_4_q, register_4_q_2, register_4_q_3, register_4_q_4;
  wire [11:0] register_3_q;
  wire [15:0] Addr, Dout, Memdout, multiplexer_1_out, multiplexer_2_out, multiplexer_3_out,
       multiplexer_4_out, multiplexer_5_out, multiplexer_6_out, Vector;

  and s2 (s2_selector, Addr[15], Addr[14], Addr[13], Addr[12], Addr[11], Addr[10], Addr[9], Addr[8], Addr[7], Addr[6], Addr[5], Addr[4], ~Addr[3], ~Addr[2], ~Addr[1], Addr[0]);  // AND_Gate
  and pb2 (pb2_selector, Addr[15], Addr[14], Addr[13], Addr[12], Addr[11], Addr[10], Addr[9], Addr[8], Addr[7], Addr[6], Addr[5], Addr[4], ~Addr[3], ~Addr[2], Addr[1], Addr[0]);  // AND_Gate
  Button pb2_2 (.out(pb2_2_out));
  Register #(.width(1)) register_1 (.D(and_1_out), .en(and_1_out), .Q(pb2Dout[0]), .clk(clk), .clr(and_2_out));
  and and_1 (and_1_out, ~pb2Dout[0], pb2_2_out);  // AND_Gate
  and and_2 (and_2_out, sseg_selector, pb2Dout[0]);
  and s1 (s1_selector, Addr[15], Addr[14], Addr[13], Addr[12], Addr[11], Addr[10], Addr[9], Addr[8], Addr[7], Addr[6], Addr[5], Addr[4], ~Addr[3], ~Addr[2], ~Addr[1], ~Addr[0]);  // AND_Gate
  and pb1 (pb1_selector, Addr[15], Addr[14], Addr[13], Addr[12], Addr[11], Addr[10], Addr[9], Addr[8], Addr[7], Addr[6], Addr[5], Addr[4], ~Addr[3], ~Addr[2], Addr[1], ~Addr[0]);  // AND_Gate
  Button pb1_2 (.out(pb1_2_out));
  Register #(.width(1)) register_2 (.D(and_3_out), .en(and_3_out), .Q(pb1Dout[0]), .clk(clk), .clr(and_4_out));
  and and_3 (and_3_out, ~pb1Dout[0], pb1_2_out);  // AND_Gate
  Clock clock_1 (.out(clk));
  and and_4 (and_4_out, sseg_selector, pb1Dout[0]);
  Multiplexer #(.width(16), .enable("false")) multiplexer_1 (
    .in0({16{1'b0}}), .in1({{15{1'b0}}, pb2Dout[0]}), .out(multiplexer_1_out), .sel(pb2_selector));
  Multiplexer #(.width(16), .enable("false")) multiplexer_2 (
    .in0(multiplexer_1_out), .in1({{15{1'b0}}, pb1Dout[0]}), .out(multiplexer_2_out), .sel(pb1_selector));
  Multiplexer #(.width(16), .enable("false")) multiplexer_3 (
    .in0(multiplexer_2_out), .in1(SB2), .out(multiplexer_3_out), .sel(s2_selector));
  and sseg (timer_selector, ~Addr[15], Addr[14], Addr[13], Addr[12], Addr[11], Addr[10], Addr[9], Addr[8], Addr[7], Addr[6], Addr[5], Addr[4], ~Addr[3], Addr[2], ~Addr[1], Addr[0]);  // AND_Gate
  and and_5 (MEMLD, ~Addr[15], memwt);  // AND_Gate
  RAM #(.addrWidth(16), .dataWidth(16), .bus("separate")) ram_1 (
    .addr(Addr), .din(Dout), .data(Memdout), .str(MEMLD), .clk(clk));  // open: sel, ld, clr
  Multiplexer #(.width(16), .enable("false")) multiplexer_4 (
    .in0(multiplexer_3_out), .in1(SB1), .out(multiplexer_4_out), .sel(s1_selector));
  Multiplexer #(.width(16), .enable("false")) multiplexer_5 (
    .in0(multiplexer_4_out), .in1(Vector), .out(multiplexer_5_out), .sel(INTACK));
  Multiplexer #(.width(16), .enable("false")) multiplexer_6 (
    .in0(Memdout), .in1(multiplexer_5_out), .out(multiplexer_6_out), .sel(Addr[15]));
  vertebrate vertebrate_1 (
    .Dout(Dout), .Din(multiplexer_6_out), .memwt(memwt), .clock(clk), .Addr(Addr), .Vector(Vector),
    .INTACK(INTACK), .test(in_3));
  and and_6 (and_6_out, sseg_selector, memwt);
  Hex_Digit_Display hex_digit_display_1 (.value(register_4_q_4));  // open: dp
  Hex_Digit_Display hex_digit_display_2 (.value(register_3_q[11:8]));  // open: dp
  Hex_Digit_Display hex_digit_display_3 (.value(register_3_q_2));  // open: dp
  Register #(.width(16)) register_3 (
    .D(Dout), .en(and_6_out), .Q({register_3_q_2, register_3_q}), .clk(clk));  // open: clr
  and sseg_2 (sseg_selector, ~Addr[15], Addr[14], Addr[13], Addr[12], Addr[11], Addr[10], Addr[9], Addr[8], Addr[7], Addr[6], Addr[5], Addr[4], ~Addr[3], Addr[2], ~Addr[1], ~Addr[0]);  // AND_Gate
  Hex_Digit_Display hex_digit_display_4 (.value(register_4_q_3));  // open: dp
  Hex_Digit_Display hex_digit_display_5 (.value(register_4_q_2));  // open: dp
  and and_7 (and_7_out, timer_selector, memwt);
  Hex_Digit_Display hex_digit_display_6 (.value(register_3_q[7:4]));  // open: dp
  Hex_Digit_Display hex_digit_display_7 (.value(register_3_q[3:0]));  // open: dp
  Hex_Digit_Display hex_digit_display_8 (.value(register_4_q));  // open: dp
  Register #(.width(16)) register_4 (
    .D(Dout), .en(and_7_out), .Q({register_4_q_4, register_4_q_3, register_4_q_2, register_4_q}), .clk(clk));  // open: clr

  // Other names for the same wires on the sheet: s1Dout[15:0] = SB1; s2Dout[15:0] = SB2
endmodule
